// Logisim project add-sub.circ as structural Verilog: 1 circuit, main circuit main
module main (
  input  [7:0] A,
  input  [7:0] B,
  input  SUB,
  input  [3:0] in_4,
  input  [3:0] in_5,
  input  in_6,
  input  [3:0] in_7,
  input  [3:0] in_8,
  output [7:0] out_9,
  output [3:0] out_10,
  output [3:0] out_11
);

  wire adder_3_cout;
  wire [3:0] bit_extender_2_out, xor_2_out, xor_3_out;
  wire [7:0] bit_extender_1_out, xor_1_out;

  assign bit_extender_1_out = {{7{SUB}}, SUB};  // Bit_Extender bit_extender_1
  assign xor_1_out = B ^ bit_extender_1_out;  // XOR_Gate xor_1, 8 bits wide
  assign bit_extender_2_out = {{3{in_6}}, in_6};  // Bit_Extender bit_extender_2
  Adder adder_1 (.a(A), .b(xor_1_out), .out(out_9), .cin(SUB));  // open: cout
  assign xor_2_out = bit_extender_2_out ^ in_7;  // XOR_Gate xor_2, 4 bits wide
  Adder #(.width(4)) adder_2 (.a(in_4), .b(xor_2_out), .out(out_10), .cin(adder_3_cout));  // open: cout
  assign xor_3_out = bit_extender_2_out ^ in_8;  // XOR_Gate xor_3, 4 bits wide
  Adder #(.width(4)) adder_3 (.a(in_5), .b(xor_3_out), .out(out_11), .cin(in_6), .cout(adder_3_cout));
endmodule
