// Logisim project alu.circ as structural Verilog: 1 circuit, main circuit main
module main (
  input  [7:0] in_1,
  input  to_data,
  input  data_to_a,
  input  a_to_one,
  input  data_to_two,
  input  sub,
  input  sum_to_data,
  output [7:0] out_8,
  output [7:0] out_9,
  output [7:0] out_10,
  output [7:0] out_11,
  output [7:0] out_12
);

  wire clk_out, rst_out;
  wire [7:0] bit_extender_1_out, controlled_buffer_2_out, controlled_buffer_3_out, controlled_buffer_5_out,
       xor_1_out;

  assign out_8 = to_data ? in_1 : 8'bz;  // Controlled_Buffer controlled_buffer_1
  Button clk (.out(clk_out));
  assign controlled_buffer_2_out = data_to_a ? out_8 : 8'bz;  // Controlled_Buffer controlled_buffer_2
  assign controlled_buffer_3_out = data_to_two ? out_8 : 8'bz;  // Controlled_Buffer controlled_buffer_3
  assign out_8 = sum_to_data ? out_12 : 8'bz;  // Controlled_Buffer controlled_buffer_4
  assign bit_extender_1_out = {{7{sub}}, sub};  // Bit_Extender bit_extender_1
  Register A (.D(controlled_buffer_2_out), .en(1'b1), .Q(out_9), .clk(clk_out), .clr(rst_out));
  Register TWO (.D(controlled_buffer_3_out), .en(1'b1), .Q(out_11), .clk(clk_out), .clr(rst_out));
  assign xor_1_out = out_11 ^ bit_extender_1_out;  // XOR_Gate xor_1, 8 bits wide
  assign controlled_buffer_5_out = a_to_one ? out_9 : 8'bz;  // Controlled_Buffer controlled_buffer_5
  Adder adder_1 (.a(out_10), .b(xor_1_out), .out(out_12), .cin(sub));  // open: cout
  Register ONE (.D(controlled_buffer_5_out), .Q(out_10), .clk(clk_out), .clr(rst_out));  // open: en
  Button rst (.out(rst_out));
endmodule
