// Logisim project cpu-prev.circ as structural Verilog: 1 circuit, main circuit main
module main (
  input  CLK_RUN,
  input  [7:0] in_2,
  input  [15:0] in_3,
  input  in_4,
  input  in_5,
  output [3:0] Microsequencer,
  output [7:0] out_7,
  output [15:0] out_8,
  output [15:0] out_9,
  output [7:0] out_10,
  output [7:0] out_11,
  output [15:0] out_12,
  output [7:0] out_13,
  output [7:0] out_14,
  output [7:0] out_15,
  output [7:0] out_16,
  output [7:0] out_17,
  output [15:0] out_18,
  output [7:0] _C_Z,
  output [7:0] out_20,
  output [7:0] out_21,
  output [7:0] out_22,
  output [15:0] out_23,
  output [7:0] out_24,
  output [7:0] out_25,
  output [15:0] out_26,
  output [7:0] out_27
);

  wire A_TO_DATA, A_TO_X, adder_1_cout, ADDR_TO_HL, ADDR_TO_IP, ADDR_TO_MAR, ADDR_TO_SP, and_1_out,
       and_2_out, B_TO_DATA, C_TO_DATA, CLK, CLK_STEP_out, clock_1_out, D_TO_DATA, DATA_TO_A, DATA_TO_B,
       DATA_TO_C, DATA_TO_D, DATA_TO_H, DATA_TO_IP_HI, DATA_TO_IP_LO, DATA_TO_IR, DATA_TO_L, DATA_TO_MAR_HI,
       DATA_TO_MAR_LO, DATA_TO_MDR, DATA_TO_SP_HI, DATA_TO_SP_LO, DATA_TO_TH, DATA_TO_TL, DATA_TO_Y, FLAGS,
       H_TO_DATA, HL_TO_ADDR, HLT, IP_HI_TO_DATA, IP_INC, IP_LO_TO_DATA, IP_TO_ADDR, L_TO_DATA, MAR_INC,
       MDR_TO_DATA, minus_CLK, nor_1_out, nor_2_out, nor_3_out, nor_4_out, nor_5_out, nor_6_out, nor_7_out,
       nor_8_out, nor_9_out, not_1_out, not_2_out, not_4_out, not_5_out, not_6_out, NXT, or_1_out, or_2_out,
       or_3_out, or_4_out, or_5_out, or_6_out, or_7_out, or_8_out, or_9_out, RST, SP_DEC, SP_HI_TO_DATA,
       SP_INC, SP_LO_TO_DATA, SP_TO_ADDR, SUB, T_TO_ADDR, TH_TO_DATA, TL_TO_DATA, Z_TO_DATA;
  wire [7:0] bit_extender_1_out, controlled_buffer_8_out, controlled_buffer_9_out, controlled_buffer_13_out,
       controlled_buffer_17_out, controlled_buffer_20_out, controlled_buffer_22_out,
       controlled_buffer_25_out, controlled_buffer_31_out, xor_1_out;
  wire [7:1] rom_1_data;
  wire [15:0] controlled_buffer_15_out;

  Button CLK_STEP (.out(CLK_STEP_out));
  Button u_RST (.out(RST));
  Clock clock_1 (.out(clock_1_out));
  and and_1 (and_1_out, clock_1_out, CLK_RUN);
  not not_1 (not_1_out, CLK_RUN);
  and and_2 (and_2_out, not_1_out, CLK_STEP_out);
  or or_1 (or_1_out, and_1_out, and_2_out);
  and and_3 (CLK, or_1_out, not_2_out);
  not not_2 (not_2_out, HLT);
  Counter #(.width(4), .max('hf)) counter_1 (
    .count(1'b1), .Q(Microsequencer), .clk(minus_CLK), .clr(or_2_out));  // open: load, D, carry
  or or_2 (or_2_out, RST, NXT);
  not not_3 (minus_CLK, CLK);
  nor nor_1 (nor_1_out, out_14[0], out_14[1], out_14[2], out_14[3], out_14[4], out_14[5], out_14[6], out_14[7]);
  D_Flip_Flop d_ff_1 (.clk(CLK), .D(nor_1_out), .Q(_C_Z[0]), .en(FLAGS), .reset(RST));  // open: Qn, preset
  D_Flip_Flop d_ff_2 (.clk(CLK), .D(adder_1_cout), .Q(_C_Z[1]), .en(FLAGS), .reset(RST));  // open: Qn, preset
  ROM #(.addrWidth(15)) rom_1 (
    .addr({Microsequencer, out_10, 1'b0, _C_Z[1:0]}), .data({rom_1_data, SP_DEC}), .sel(1'b1));
  Register register_1 (.D(out_7), .en(DATA_TO_IR), .Q(out_10), .clk(CLK), .clr(RST));
  Register register_2 (.D(out_7), .en(DATA_TO_A), .Q(out_11), .clk(CLK));  // open: clr
  Register register_3 (.D(out_11), .en(A_TO_X), .Q(out_13), .clk(CLK));  // open: clr
  assign bit_extender_1_out = {{7{SUB}}, SUB};  // Bit_Extender bit_extender_1
  assign xor_1_out = bit_extender_1_out ^ out_20;  // XOR_Gate xor_1, 8 bits wide
  Register register_4 (.D(out_7), .en(DATA_TO_Y), .Q(out_20), .clk(CLK));  // open: clr
  Register register_5 (.D(out_7), .en(DATA_TO_B), .Q(out_24), .clk(CLK));  // open: clr
  Register register_6 (.D(out_7), .en(DATA_TO_C), .Q(out_25), .clk(CLK));  // open: clr
  Register register_7 (.D(out_7), .en(DATA_TO_D), .Q(out_27), .clk(CLK));  // open: clr
  assign out_7 = A_TO_DATA ? out_11 : 8'bz;  // Controlled_Buffer controlled_buffer_1
  Adder adder_1 (.a(out_13), .b(xor_1_out), .out(out_14), .cin(SUB), .cout(adder_1_cout));
  assign out_7 = B_TO_DATA ? out_24 : 8'bz;  // Controlled_Buffer controlled_buffer_2
  assign out_7 = C_TO_DATA ? out_25 : 8'bz;  // Controlled_Buffer controlled_buffer_3
  assign out_7 = D_TO_DATA ? out_27 : 8'bz;  // Controlled_Buffer controlled_buffer_4
  ROM #(.addrWidth(15)) rom_2 (
    .addr({Microsequencer, out_10, 1'b0, _C_Z[1:0]}),
    .data({SP_INC, SP_TO_ADDR, ADDR_TO_SP, SP_LO_TO_DATA, DATA_TO_SP_LO, SP_HI_TO_DATA, DATA_TO_SP_HI, T_TO_ADDR}),
    .sel(1'b1));
  assign out_7 = Z_TO_DATA ? out_14 : 8'bz;  // Controlled_Buffer controlled_buffer_5
  assign out_7 = in_4 ? in_2 : 8'bz;  // Controlled_Buffer controlled_buffer_6
  assign out_7 = IP_LO_TO_DATA ? out_9[7:0] : 8'bz;  // Controlled_Buffer controlled_buffer_7
  assign controlled_buffer_8_out = DATA_TO_IP_LO ? out_7 : 8'bz;  // Controlled_Buffer controlled_buffer_8
  assign controlled_buffer_9_out = DATA_TO_MAR_LO ? out_7 : 8'bz;  // Controlled_Buffer controlled_buffer_9
  assign out_15 = DATA_TO_MDR ? out_7 : 8'bz;  // Controlled_Buffer controlled_buffer_10
  assign out_7 = MDR_TO_DATA ? out_15 : 8'bz;  // Controlled_Buffer controlled_buffer_11
  assign out_7 = L_TO_DATA ? out_17 : 8'bz;  // Controlled_Buffer controlled_buffer_12
  assign controlled_buffer_13_out = DATA_TO_L ? out_7 : 8'bz;  // Controlled_Buffer controlled_buffer_13
  assign out_7 = TL_TO_DATA ? out_22 : 8'bz;  // Controlled_Buffer controlled_buffer_14
  assign controlled_buffer_15_out[7:0] = DATA_TO_TL ? out_7 : 8'bz;  // Controlled_Buffer controlled_buffer_15
  assign out_7 = SP_LO_TO_DATA ? out_26[7:0] : 8'bz;  // Controlled_Buffer controlled_buffer_16
  assign controlled_buffer_17_out = DATA_TO_SP_LO ? out_7 : 8'bz;  // Controlled_Buffer controlled_buffer_17
  ROM #(.addrWidth(15)) rom_3 (
    .addr({Microsequencer, out_10, 1'b0, _C_Z[1:0]}),
    .data({TL_TO_DATA, DATA_TO_TL, TH_TO_DATA, DATA_TO_TH, HL_TO_ADDR, ADDR_TO_HL, L_TO_DATA, DATA_TO_L}),
    .sel(1'b1));
  assign out_7 = IP_HI_TO_DATA ? out_9[15:8] : 8'bz;  // Controlled_Buffer controlled_buffer_18
  nor nor_2 (nor_2_out, DATA_TO_IP_LO, ADDR_TO_IP);
  assign controlled_buffer_8_out = nor_2_out ? out_9[7:0] : 8'bz;  // Controlled_Buffer controlled_buffer_19
  assign controlled_buffer_20_out = DATA_TO_IP_HI ? out_7 : 8'bz;  // Controlled_Buffer controlled_buffer_20
  nor nor_3 (nor_3_out, DATA_TO_MAR_LO, ADDR_TO_MAR);
  assign controlled_buffer_9_out = nor_3_out ? out_12[7:0] : 8'bz;  // Controlled_Buffer controlled_buffer_21
  assign controlled_buffer_22_out = DATA_TO_MAR_HI ? out_7 : 8'bz;  // Controlled_Buffer controlled_buffer_22
  not not_4 (not_4_out, DATA_TO_MDR);
  assign out_7 = H_TO_DATA ? out_16 : 8'bz;  // Controlled_Buffer controlled_buffer_23
  nor nor_4 (nor_4_out, DATA_TO_L, ADDR_TO_HL);
  assign controlled_buffer_13_out = nor_4_out ? out_17 : 8'bz;  // Controlled_Buffer controlled_buffer_24
  assign controlled_buffer_25_out = DATA_TO_H ? out_7 : 8'bz;  // Controlled_Buffer controlled_buffer_25
  assign out_7 = TH_TO_DATA ? out_21 : 8'bz;  // Controlled_Buffer controlled_buffer_26
  not not_5 (not_5_out, DATA_TO_TH);
  not not_6 (not_6_out, DATA_TO_TL);
  assign controlled_buffer_15_out[7:0] = not_6_out ? out_22 : 8'bz;  // Controlled_Buffer controlled_buffer_27
  assign controlled_buffer_15_out[15:8] = DATA_TO_TH ? out_7 : 8'bz;  // Controlled_Buffer controlled_buffer_28
  assign out_7 = SP_HI_TO_DATA ? out_26[15:8] : 8'bz;  // Controlled_Buffer controlled_buffer_29
  nor nor_5 (nor_5_out, DATA_TO_SP_LO, ADDR_TO_SP);
  assign controlled_buffer_17_out = nor_5_out ? out_26[7:0] : 8'bz;  // Controlled_Buffer controlled_buffer_30
  assign controlled_buffer_31_out = DATA_TO_SP_HI ? out_7 : 8'bz;  // Controlled_Buffer controlled_buffer_31
  nor nor_6 (nor_6_out, DATA_TO_IP_HI, ADDR_TO_IP);
  assign controlled_buffer_20_out = nor_6_out ? out_9[15:8] : 8'bz;  // Controlled_Buffer controlled_buffer_32
  or or_3 (or_3_out, DATA_TO_IP_HI, DATA_TO_IP_LO, ADDR_TO_IP);
  nor nor_7 (nor_7_out, DATA_TO_MAR_HI, ADDR_TO_MAR);
  assign controlled_buffer_22_out = nor_7_out ? out_12[15:8] : 8'bz;  // Controlled_Buffer controlled_buffer_33
  or or_4 (or_4_out, DATA_TO_MAR_HI, DATA_TO_MAR_LO, ADDR_TO_MAR);
  nor nor_8 (nor_8_out, DATA_TO_H, ADDR_TO_HL);
  assign controlled_buffer_25_out = nor_8_out ? out_16 : 8'bz;  // Controlled_Buffer controlled_buffer_34
  or or_5 (or_5_out, DATA_TO_H, DATA_TO_L, ADDR_TO_HL);
  assign controlled_buffer_15_out[15:8] = not_5_out ? out_21 : 8'bz;  // Controlled_Buffer controlled_buffer_35
  or or_6 (or_6_out, DATA_TO_TH, DATA_TO_TL);
  nor nor_9 (nor_9_out, DATA_TO_SP_HI, ADDR_TO_SP);
  assign controlled_buffer_31_out = nor_9_out ? out_26[15:8] : 8'bz;  // Controlled_Buffer controlled_buffer_36
  or or_7 (or_7_out, DATA_TO_SP_HI, DATA_TO_SP_LO, ADDR_TO_SP);
  ROM #(.addrWidth(15)) rom_4 (
    .addr({Microsequencer, out_10, 1'b0, _C_Z[1:0]}),
    .data({H_TO_DATA, DATA_TO_H, MDR_TO_DATA, DATA_TO_MDR, MAR_INC, ADDR_TO_MAR, DATA_TO_MAR_LO, DATA_TO_MAR_HI}),
    .sel(1'b1));
  Register #(.width(16)) register_8 (
    .D(controlled_buffer_15_out), .en(or_6_out), .Q({out_21, out_22}), .clk(CLK), .clr(RST));
  or or_8 (or_8_out, or_7_out, SP_DEC);
  or or_9 (or_9_out, SP_DEC, SP_INC);
  Counter #(.width(16), .max('hffff)) counter_2 (
    .load(or_3_out), .D({controlled_buffer_20_out, controlled_buffer_8_out}), .count(IP_INC), .Q(out_9),
    .clk(CLK), .clr(RST));  // open: carry
  Counter #(.width(16), .max('hffff)) counter_3 (
    .load(or_4_out), .D({controlled_buffer_22_out, controlled_buffer_9_out}), .count(MAR_INC), .Q(out_12),
    .clk(CLK));  // open: carry, clr
  Register #(.width(16)) register_9 (
    .D({controlled_buffer_25_out, controlled_buffer_13_out}), .en(or_5_out), .Q({out_16, out_17}), .clk(CLK),
    .clr(RST));
  Counter #(.width(16), .max('hffff)) counter_4 (
    .load(or_8_out), .D({controlled_buffer_31_out, controlled_buffer_17_out}), .count(or_9_out), .Q(out_26),
    .clk(CLK), .clr(RST));  // open: carry
  ROM #(.addrWidth(15)) rom_5 (
    .addr({Microsequencer, out_10, 1'b0, _C_Z[1:0]}),
    .data({IP_INC, IP_TO_ADDR, ADDR_TO_IP, IP_LO_TO_DATA, DATA_TO_IP_LO, IP_HI_TO_DATA, DATA_TO_IP_HI, D_TO_DATA}),
    .sel(1'b1));
  RAM #(.addrWidth(16)) ram_1 (.addr(out_12), .data(out_15), .sel(1'b1), .clk(CLK), .ld(not_4_out));  // open: clr
  ROM #(.addrWidth(15)) rom_6 (
    .addr({Microsequencer, out_10, 1'b0, _C_Z[1:0]}),
    .data({DATA_TO_D, C_TO_DATA, DATA_TO_C, B_TO_DATA, DATA_TO_B, Z_TO_DATA, FLAGS, SUB}), .sel(1'b1));
  assign out_8 = in_5 ? in_3 : 16'bz;  // Controlled_Buffer controlled_buffer_37
  assign out_8 = IP_TO_ADDR ? out_9 : 16'bz;  // Controlled_Buffer controlled_buffer_38
  assign {controlled_buffer_20_out, controlled_buffer_8_out} = ADDR_TO_IP ? out_8 : 16'bz;  // Controlled_Buffer controlled_buffer_39
  assign {controlled_buffer_22_out, controlled_buffer_9_out} = ADDR_TO_MAR ? out_8 : 16'bz;  // Controlled_Buffer controlled_buffer_40
  assign out_8 = HL_TO_ADDR ? {out_16, out_17} : 16'bz;  // Controlled_Buffer controlled_buffer_41
  assign {controlled_buffer_25_out, controlled_buffer_13_out} = ADDR_TO_HL ? out_8 : 16'bz;  // Controlled_Buffer controlled_buffer_42
  assign out_8 = T_TO_ADDR ? {out_21, out_22} : 16'bz;  // Controlled_Buffer controlled_buffer_43
  assign out_8 = SP_TO_ADDR ? out_26 : 16'bz;  // Controlled_Buffer controlled_buffer_44
  assign {controlled_buffer_31_out, controlled_buffer_17_out} = ADDR_TO_SP ? out_8 : 16'bz;  // Controlled_Buffer controlled_buffer_45
  ROM #(.addrWidth(15)) rom_7 (
    .addr({Microsequencer, out_10, 1'b0, _C_Z[1:0]}),
    .data({DATA_TO_Y, A_TO_X, A_TO_DATA, DATA_TO_A, DATA_TO_IR, NXT, RST, HLT}), .sel(1'b1));

  assign _C_Z[7:2] = {6{1'b0}};
  assign out_18 = {out_16, out_17};
  assign out_23 = {out_21, out_22};

  // Other names for the same wires on the sheet: ZF = _C_Z[0]; CF = _C_Z[1]

  // Notes on the sheet:
  //   Clock
  //   Adder / Substractor
  //   Flags
  //   Control Unit
  //   Instruction Register
  //   A Register
  //   X Register
  //   Y Register
  //   B Register
  //   C Register
  //   D Register
  //   48-55
  //   40-47
  //   Z Register
  //   8-Bit Data Bus
  //   32-39
  //   24-31
  //   TH Register
  //   TL Register
  //   T Register
  //   16-23
  //   Instruction Pointer
  //   Memory Address Register
  //   H Register
  //   L Register
  //   HL Register
  //   Stack Pointer
  //   Memory Data Register
  //   8-15
  //   0-7
  //   16-Bit Address Bus
endmodule
