// Logisim project cpu.circ as structural Verilog: 1 circuit, main circuit main
module main (
  input  CLK_RUN,
  input  [7:0] in_2,
  input  [15:0] in_3,
  input  in_4,
  input  in_5,
  output [3:0] out_6,
  output [7:0] out_7,
  output [15:0] out_8,
  output [15:0] out_9,
  output [7:0] out_10,
  output [7:0] out_11,
  output [15:0] out_12,
  output [7:0] out_13,
  output [7:0] out_14,
  output [7:0] out_15,
  output [7:0] out_16,
  output [7:0] out_17,
  output [15:0] out_18,
  output [7:0] _C_Z,
  output [15:0] out_20,
  output [7:0] out_21,
  output [7:0] out_22,
  output [15:0] out_23,
  output [7:0] out_24,
  output [7:0] out_25
);

  wire A_TO_DATA, A_TO_X, adder_1_cout, adder_2_cout, ADDR_HI_TO_DATA, ADDR_LO_TO_DATA, ADDR_TO_HL,
       ADDR_TO_IP, ADDR_TO_MAR, ADDR_TO_SP, ADDR_TO_T, and_1_out, and_2_out, and_4_out, and_5_out, and_6_out,
       and_7_out, and_8_out, and_9_out, and_10_out, and_11_out, and_12_out, B_TO_DATA, C_TO_DATA, CARRY, CLK,
       CLK_STEP_out, clock_1_out, D_TO_DATA, DATA_TO_A, DATA_TO_ADDR_HI, DATA_TO_ADDR_LO, DATA_TO_B,
       DATA_TO_C, DATA_TO_D, DATA_TO_FLAGS, DATA_TO_IR, DATA_TO_MDR, DATA_TO_X, DATA_TO_Y, decoder_1_out0,
       decoder_1_out1, FLAGS, FLAGS_TO_DATA, H_TO_DATA, HL_TO_ADDR, HLT, HRST_out, IP_INC, IP_TO_ADDR,
       L_TO_DATA, MAR_INC, MDR_TO_DATA, minus_CLK, nor_2_out, not_1_out, not_2_out, not_3_out, not_5_out,
       not_6_out, not_7_out, NXT, or_2_out, or_3_out, or_4_out, or_5_out, or_6_out, or_7_out, or_8_out,
       or_9_out, or_10_out, or_11_out, or_12_out, or_13_out, or_14_out, RST, SP_DEC, SP_INC, SP_TO_ADDR,
       SRST, SUB, T_RST, T_TO_ADDR, xor_1_out, xor_5_out, Y_RST, Z_TO_DATA;
  wire [1:0] nor_1_out;
  wire [2:0] rom_1_data, rom_2_data, rom_2_data_3, rom_3_data;
  wire [3:0] bit_extender_1_out, xor_2_out, xor_4_out;
  wire [5:3] rom_2_data_2;
  wire [7:0] multiplexer_1_out, multiplexer_2_out, register_8_q, rom_4_data;

  Button CLK_STEP (.out(CLK_STEP_out));
  Button HRST (.out(HRST_out));
  Clock clock_1 (.out(clock_1_out));
  and and_1 (and_1_out, clock_1_out, CLK_RUN);
  not not_1 (not_1_out, CLK_RUN);
  and and_2 (and_2_out, not_1_out, CLK_STEP_out);
  or or_1 (RST, HRST_out, SRST);
  not not_2 (not_2_out, NXT);
  or or_2 (or_2_out, and_1_out, and_2_out);
  not not_3 (not_3_out, HLT);
  Demultiplexer #(.select(3), .enable("false")) demultiplexer_1 (
    .out1(Z_TO_DATA), .out2(H_TO_DATA), .out3(L_TO_DATA), .out4(FLAGS), .out5(T_RST), .out6(HLT), .out7(NXT),
    .in(1'b1), .sel(rom_1_data));  // open: out0
  Counter #(.width(4), .max('hf)) counter_1 (
    .load(NXT), .D(4'b0000), .count(not_2_out), .Q(out_6), .clk(minus_CLK), .clr(RST));  // open: carry
  not not_4 (minus_CLK, CLK);
  and and_3 (CLK, or_2_out, not_3_out);
  Multiplexer #(.width(8), .enable("false")) multiplexer_1 (
    .in0(out_7), .in1(out_11), .out(multiplexer_1_out), .sel(A_TO_X));
  xor xor_1 (xor_1_out, CARRY, SUB);
  assign bit_extender_1_out = {{3{SUB}}, SUB};  // Bit_Extender bit_extender_1
  assign xor_2_out = bit_extender_1_out ^ out_21[7:4];  // XOR_Gate xor_2, 4 bits wide
  ROM #(.addrWidth(15)) rom_1 (
    .addr({1'b0, _C_Z[1:0], out_6, out_10}), .data({rom_1_data, CARRY, SUB, DATA_TO_Y, DATA_TO_X, A_TO_X}),
    .sel(1'b1));
  Register register_1 (.D(out_7), .en(DATA_TO_IR), .Q(out_10), .clk(CLK), .clr(RST));
  Register register_2 (.D(out_7), .en(DATA_TO_A), .Q(out_11), .clk(CLK));  // open: clr
  Register register_3 (.D(multiplexer_1_out), .en(or_3_out), .Q(out_13), .clk(CLK));  // open: clr
  or or_3 (or_3_out, A_TO_X, DATA_TO_X);
  Adder #(.width(4)) adder_1 (
    .a(out_13[7:4]), .b(xor_2_out), .out(out_14[7:4]), .cin(adder_2_cout), .cout(adder_1_cout));
  Register register_4 (.D(out_7), .en(DATA_TO_Y), .Q(out_21), .clk(CLK), .clr(Y_RST));
  Register register_5 (.D(out_7), .en(DATA_TO_B), .Q(out_22), .clk(CLK));  // open: clr
  Register register_6 (.D(out_7), .en(DATA_TO_C), .Q(out_24), .clk(CLK));  // open: clr
  Register register_7 (.D(out_7), .en(DATA_TO_D), .Q(out_25), .clk(CLK));  // open: clr
  assign out_7 = A_TO_DATA ? out_11 : 8'bz;  // Controlled_Buffer controlled_buffer_1
  Adder #(.width(4)) adder_2 (.a(out_13[3:0]), .b(xor_4_out), .out(out_14[3:0]), .cin(xor_1_out), .cout(adder_2_cout));
  xor xor_3 (nor_1_out[1], adder_1_cout, SUB);
  nor nor_1 (nor_1_out[0], out_14[0], out_14[1], out_14[2], out_14[3], out_14[4], out_14[5], out_14[6], out_14[7]);
  assign xor_4_out = bit_extender_1_out ^ out_21[3:0];  // XOR_Gate xor_4, 4 bits wide
  or or_4 (or_4_out, DATA_TO_FLAGS, FLAGS);
  assign out_7 = B_TO_DATA ? out_22 : 8'bz;  // Controlled_Buffer controlled_buffer_2
  assign out_7 = C_TO_DATA ? out_24 : 8'bz;  // Controlled_Buffer controlled_buffer_3
  assign out_7 = D_TO_DATA ? out_25 : 8'bz;  // Controlled_Buffer controlled_buffer_4
  Demultiplexer #(.select(3), .enable("false")) demultiplexer_2 (
    .out1(DATA_TO_A), .out2(DATA_TO_B), .out3(DATA_TO_C), .out4(DATA_TO_D), .out5(DATA_TO_MDR),
    .out6(DATA_TO_ADDR_HI), .out7(DATA_TO_ADDR_LO), .in(1'b1), .sel(rom_2_data));  // open: out0
  assign out_7 = Z_TO_DATA ? out_14 : 8'bz;  // Controlled_Buffer controlled_buffer_5
  Register register_8 (.D({{6{1'b0}}, nor_1_out}), .en(Z_TO_DATA), .Q(register_8_q), .clk(CLK));  // open: clr
  Multiplexer #(.width(8), .enable("false")) multiplexer_2 (
    .in0({{6{1'b0}}, register_8_q[1:0]}), .in1(out_7), .out(multiplexer_2_out), .sel(DATA_TO_FLAGS));
  assign out_7 = FLAGS_TO_DATA ? _C_Z : 8'bz;  // Controlled_Buffer controlled_buffer_6
  Register register_9 (.D(multiplexer_2_out), .en(or_4_out), .Q(_C_Z), .clk(CLK), .clr(RST));
  ROM #(.addrWidth(15)) rom_2 (
    .addr({1'b0, _C_Z[1:0], out_6, out_10}), .data({rom_2_data_3[1:0], rom_2_data_2, rom_2_data}), .sel(1'b1));
  assign out_7 = in_4 ? in_2 : 8'bz;  // Controlled_Buffer controlled_buffer_7
  assign out_7 = MDR_TO_DATA ? out_15 : 8'bz;  // Controlled_Buffer controlled_buffer_8
  assign out_7 = L_TO_DATA ? out_16 : 8'bz;  // Controlled_Buffer controlled_buffer_9
  assign out_7 = H_TO_DATA ? out_17 : 8'bz;  // Controlled_Buffer controlled_buffer_10
  assign out_8[7:0] = DATA_TO_ADDR_LO ? out_7 : 8'bz;  // Controlled_Buffer controlled_buffer_11
  assign out_8[15:8] = DATA_TO_ADDR_HI ? out_7 : 8'bz;  // Controlled_Buffer controlled_buffer_12
  Demultiplexer #(.select(3), .enable("false")) demultiplexer_3 (
    .out1(A_TO_DATA), .out2(B_TO_DATA), .out3(C_TO_DATA), .out4(D_TO_DATA), .out5(MDR_TO_DATA),
    .out6(ADDR_HI_TO_DATA), .out7(ADDR_LO_TO_DATA), .in(1'b1), .sel(rom_2_data_2));  // open: out0
  ROM #(.addrWidth(15)) rom_3 (
    .addr({1'b0, _C_Z[1:0], out_6, out_10}),
    .data({DATA_TO_FLAGS, FLAGS_TO_DATA, SP_INC, SP_DEC, rom_3_data, rom_2_data_3[2]}), .sel(1'b1));
  Counter #(.width(16), .max('hffff)) counter_2 (
    .load(ADDR_TO_IP), .D(out_8), .count(IP_INC), .Q(out_9), .clk(CLK), .clr(RST));  // open: carry
  Counter #(.width(16), .max('hffff)) counter_3 (
    .load(ADDR_TO_MAR), .D(out_8), .count(MAR_INC), .Q(out_12), .clk(CLK));  // open: carry, clr
  or or_5 (or_5_out, ADDR_TO_SP, SP_DEC);
  or or_6 (or_6_out, SP_DEC, SP_INC);
  Decoder #(.disabled(0), .enable("false")) decoder_1 (.out0(decoder_1_out0), .out1(decoder_1_out1), .sel(out_12[15]));
  Register #(.width(16)) register_10 (.D(out_8), .en(ADDR_TO_T), .Q(out_20), .clk(CLK), .clr(T_RST));
  Counter #(.width(16), .max('hffff)) counter_4 (
    .load(or_5_out), .D(out_8), .count(or_6_out), .Q(out_23), .clk(CLK), .clr(RST));  // open: carry
  Demultiplexer #(.select(3), .enable("false")) demultiplexer_4 (
    .out1(ADDR_TO_IP), .out2(ADDR_TO_HL), .out3(ADDR_TO_T), .out4(ADDR_TO_SP), .out5(MAR_INC),
    .out6(ADDR_TO_MAR), .out7(DATA_TO_IR), .in(1'b1), .sel(rom_2_data_3));  // open: out0
  and and_4 (and_4_out, ADDR_TO_IP, DATA_TO_ADDR_HI);
  or or_7 (or_7_out, and_4_out, IP_TO_ADDR);
  and and_5 (and_5_out, ADDR_TO_IP, DATA_TO_ADDR_LO);
  or or_8 (or_8_out, IP_TO_ADDR, and_5_out);
  nor nor_2 (nor_2_out, out_12[11], out_12[12], out_12[13], out_12[14], out_12[15]);
  xor xor_5 (xor_5_out, nor_2_out, decoder_1_out0);
  not not_5 (not_5_out, nor_2_out);
  Register #(.width(16)) register_11 (.D(out_8), .en(ADDR_TO_HL), .Q({out_17, out_16}), .clk(CLK));  // open: clr
  assign out_8[7:0] = or_7_out ? out_9[7:0] : 8'bz;  // Controlled_Buffer controlled_buffer_13
  assign out_8[15:8] = or_8_out ? out_9[15:8] : 8'bz;  // Controlled_Buffer controlled_buffer_14
  and and_6 (and_6_out, not_5_out, DATA_TO_MDR);
  not not_6 (not_6_out, and_6_out);
  assign out_15 = and_6_out ? out_7 : 8'bz;  // Controlled_Buffer controlled_buffer_15
  and and_7 (and_7_out, ADDR_TO_T, DATA_TO_ADDR_HI);
  and and_8 (and_8_out, ADDR_TO_T, DATA_TO_ADDR_LO);
  and and_9 (and_9_out, ADDR_TO_SP, DATA_TO_ADDR_HI);
  and and_10 (and_10_out, ADDR_TO_SP, DATA_TO_ADDR_LO);
  ROM #(.addrWidth(11)) rom_4 (.addr(out_12[10:0]), .data(rom_4_data), .sel(nor_2_out));
  not not_7 (not_7_out, DATA_TO_MDR);
  assign out_15 = not_7_out ? rom_4_data : 8'bz;  // Controlled_Buffer controlled_buffer_16
  RAM #(.addrWidth(15)) ram_1 (
    .addr(out_12[14:0]), .data(out_15), .sel(xor_5_out), .clk(CLK), .ld(not_6_out));  // open: clr
  and and_11 (and_11_out, ADDR_TO_HL, DATA_TO_ADDR_HI);
  and and_12 (and_12_out, ADDR_TO_HL, DATA_TO_ADDR_LO);
  assign out_8[7:0] = or_9_out ? out_20[7:0] : 8'bz;  // Controlled_Buffer controlled_buffer_17
  assign out_8[15:8] = or_10_out ? out_20[15:8] : 8'bz;  // Controlled_Buffer controlled_buffer_18
  or or_9 (or_9_out, and_7_out, T_TO_ADDR);
  or or_10 (or_10_out, T_TO_ADDR, and_8_out);
  assign out_8[7:0] = or_11_out ? out_23[7:0] : 8'bz;  // Controlled_Buffer controlled_buffer_19
  assign out_8[15:8] = or_12_out ? out_23[15:8] : 8'bz;  // Controlled_Buffer controlled_buffer_20
  or or_11 (or_11_out, and_9_out, SP_TO_ADDR);
  or or_12 (or_12_out, SP_TO_ADDR, and_10_out);
  assign out_8[7:0] = or_13_out ? out_16 : 8'bz;  // Controlled_Buffer controlled_buffer_21
  assign out_8[15:8] = or_14_out ? out_17 : 8'bz;  // Controlled_Buffer controlled_buffer_22
  or or_13 (or_13_out, and_11_out, HL_TO_ADDR);
  or or_14 (or_14_out, HL_TO_ADDR, and_12_out);
  Demultiplexer #(.select(3), .enable("false")) demultiplexer_5 (
    .out1(IP_TO_ADDR), .out2(HL_TO_ADDR), .out3(T_TO_ADDR), .out4(SP_TO_ADDR), .out5(IP_INC), .out6(Y_RST),
    .out7(SRST), .in(1'b1), .sel(rom_3_data));  // open: out0
  RAM #(.addrWidth(15)) ram_2 (
    .addr(out_12[14:0]), .data(out_15), .sel(decoder_1_out1), .clk(CLK), .ld(not_6_out));  // open: clr
  assign out_7 = ADDR_LO_TO_DATA ? out_8[7:0] : 8'bz;  // Controlled_Buffer controlled_buffer_23
  assign out_7 = ADDR_HI_TO_DATA ? out_8[15:8] : 8'bz;  // Controlled_Buffer controlled_buffer_24
  assign out_8 = in_5 ? in_3 : 16'bz;  // Controlled_Buffer controlled_buffer_25

  assign out_18 = {out_17, out_16};

  // Other names for the same wires on the sheet: ZF = _C_Z[0]; CF = _C_Z[1]

  // Notes on the sheet:
  //   Microsequencer
  //   Control Unit
  //   Clock
  //   Instruction Register
  //   A Register
  //   X Register
  //   Y Register
  //   B Register
  //   C Register
  //   D Register
  //   Adder / Subtractor
  //   0-7
  //   contents of rom_1 (hex, n*v repeats v):
  //   512*0 e0 5*0 e0 10*0 e0 4*0 e0 10*0 e0 46*0 6*5 0 0 6*5 0 0 8*5 45 45 65 65 4*0 5 0 5 0 5 0 5 0 45
  //   e0 65 10*0 e0 0 0 40 0 60 4*0 e0 7*0 62 40 0 60 12*0 62 40 0 60 13*0 40 0 60 10*0 e0 4*0 60 6*0 e0
  //   6*0 40 23*0 1 2 2 2 42 62 0 0 1 2 2 2 42 62 0 c0 0 e0 e0 0 e0 11*0 e0 0 0 0 e0 11*0 e0 0 e0 45*0
  //   6*20 5 5 6*28 5 5 20 28 20 28 20 28 20 28 20 28 20 28 4*5 28 0 28 0 28 e0 28 0 28 0 28 0 5 e0 5 0 0
  //   0 e0 0 e0 0 e0 0 e0 0 e0 5*0 e0 0 0 0 e0 0 e0 30 e0 0 e0 5*0 e0 0 e0 0 0 0 e0 38 e0 0 e0 4*0 e0 e0 0
  //   e0 0 e0 0 0 0 e0 0 e0 5*0 e0 0 e0 0 e0 0 e0 0 0 0 e0 5*0 e0 0 e0 0 e0 0 e0 0 e0 6*0 a6 8*0 40 0 60
  //   5*0 6*30 2 0 6*38 2 8*0 e0 15*0 e0 56*0 6*80 20 20 6*80 28 28 12*80 20 28 20 28 80 0 80 0 80 0 80 0
  //   80 0 80 e0 28 0 28 0 0 e0 10*0 e0 0 e0 4*0 e0 0 0 0 80 4*0 e0 0 e0 e0 5*0 e0 0 80 4*0 e0 0 e0 8*0 e0
  //   4*0 e0 0 e0 8*0 e0 40 e0 0 0 e0 0 e0 4*0 e0 5*0 e0 60 e0 e0 0 e0 20 e0 0 e0 0 e0 0 e0 0 e0 0 e0 5*0
  //   6*80 30 0 6*80 38 81*0 6*e0 80 80 6*e0 80 80 12*e0 4*80 e0 0 e0 0 e0 0 e0 0 e0 0 e0 0 80 0 80 0 e0
  //   6*0 e0 10*0 e0 4*0 e0 12*0 e0 0 0 e0 14*0 e0 17*0 e0 17*0 e0 4*0 6 16*0 6*e0 80 0 6*e0 80 4*0 e0 0
  //   e0 8*0 e0 6*0 e0 8*0 e0 4*0 e0 10*0 e0 39*0 e0 e0 6*0 e0 e0 12*0 4*e0 7*0 e0 4*0 e0 0 e0 e0 0 0 0 e0
  //   17*0 e0 41*0 e0 31*0 20 22*0 e0 7*0 e0 146*0 e0 87*0 40 0 60 38*0 e0 122*0 e0 9*0 e0 5*0 e0 9*0 e0
  //   5*0 e0 7*0 e0 7*0 e0 0 0 0 e0 9*0 e0 0 e0 7*0 e0 7*0 e0 0 0 0 e0 0 e0 0 e0 0 e0 0 e0 0 e0 551*0 e0
  //   175*0 e0 11*0 e0 7*0 e0 775*0 e0 800*0 e0 e0 15*0 e0 e0 16*0 e0 44*0 6*5 0 0 6*5 0 0 8*5 45 45 65 65
  //   4*0 5 0 5 0 5 0 5 0 45 e0 65 8*0 e0 4*0 40 0 60 12*0 62 40 0 60 12*0 62 40 0 60 4*0 e0 8*0 40 0 60
  //   10*0 e0 4*0 60 10*0 e0 0 0 40 23*0 1 2 2 2 42 62 0 0 1 2 2 2 42 62 0 c0 0 0 e0 0 e0 0 e0 9*0 e0 0 0
  //   0 e0 11*0 e0 0 e0 45*0 6*20 5 5 6*28 5 5 20 28 20 28 20 28 20 28 20 28 20 28 4*5 28 0 28 0 28 e0 28
  //   0 28 0 28 0 5 e0 5 0 0 0 e0 0 e0 0 e0 0 e0 0 e0 4*0 e0 e0 0 0 0 e0 0 e0 30 e0 0 e0 5*0 e0 0 e0 0 0 0
  //   e0 38 e0 0 e0 5*0 e0 0 e0 0 e0 0 0 0 e0 0 e0 5*0 e0 0 e0 0 e0 0 e0 0 0 0 e0 5*0 e0 0 e0 0 e0 0 e0 0
  //   e0 6*0 a6 8*0 40 0 60 5*0 6*30 2 0 6*38 2 4*0 e0 15*0 e0 60*0 6*80 20 20 6*80 28 28 12*80 20 28 20
  //   28 80 0 80 0 80 0 80 0 80 0 80 e0 28 0 28 0 0 e0 10*0 e0 0 e0 4*0 e0 0 0 0 80 4*0 e0 0 e0 6*0 e0 0
  //   80 4*0 e0 0 e0 8*0 e0 4*0 e0 0 e0 e0 7*0 e0 40 e0 0 0 e0 0 e0 8*0 e0 0 e0 60 e0 e0 0 e0 20 e0 0 e0 0
  //   e0 0 e0 0 e0 0 e0 5*0 6*80 30 0 6*80 38 81*0 6*e0 80 80 6*e0 80 80 12*e0 4*80 e0 0 e0 0 e0 0 e0 0 e0
  //   0 e0 0 80 0 80 0 e0 6*0 e0 10*0 e0 4*0 e0 12*0 e0 0 0 e0 14*0 e0 17*0 e0 17*0 e0 4*0 6 16*0 6*e0 80
  //   0 6*e0 80 6*0 e0 0 e0 6*0 e0 6*0 e0 8*0 e0 0 0 e0 12*0 e0 39*0 e0 e0 6*0 e0 e0 12*0 4*e0 7*0 e0 4*0
  //   e0 0 e0 e0 5*0 e0 15*0 e0 9*0 e0 63*0 20 22*0 e0 7*0 e0 146*0 e0 87*0 40 0 60 42*0 e0 118*0 e0 9*0
  //   e0 5*0 e0 9*0 e0 5*0 e0 7*0 e0 7*0 e0 0 0 0 e0 9*0 e0 0 e0 0 0 0 e0 11*0 e0 0 0 0 e0 0 e0 0 e0 0 e0
  //   0 e0 0 e0 555*0 e0 171*0 e0 11*0 e0 0 0 0 e0 779*0 e0 800*0 e0 e0 16*0 e0 0 0 e0 11*0 e0 46*0 6*5 0
  //   0 6*5 0 0 8*5 45 45 65 65 4*0 5 0 5 0 5 0 5 0 45 0 65 0 0 e0 5*0 e0 4*0 40 0 60 4*0 e0 7*0 62 40 0
  //   60 12*0 62 40 0 60 13*0 40 0 60 15*0 60 e0 5*0 e0 6*0 40 23*0 1 2 2 2 42 62 0 0 1 2 2 2 42 62 0 c0 0
  //   0 e0 0 e0 0 e0 9*0 e0 0 0 0 e0 11*0 e0 0 e0 45*0 6*30 5 5 6*38 5 5 20 28 20 28 20 28 20 28 20 28 20
  //   28 4*5 28 0 28 0 28 e0 28 0 28 e0 28 0 5 0 5 0 0 0 e0 0 e0 0 e0 0 e0 0 e0 5*0 e0 0 0 0 e0 0 e0 30 e0
  //   0 e0 5*0 e0 0 e0 0 0 0 e0 38 e0 0 e0 4*0 e0 e0 0 e0 0 e0 0 0 0 e0 0 e0 5*0 e0 0 e0 0 e0 0 e0 0 0 0
  //   e0 5*0 e0 0 e0 0 e0 0 e0 0 e0 6*0 a6 8*0 40 0 60 5*0 6*30 2 0 6*38 2 4*0 e0 15*0 e0 60*0 6*80 30 30
  //   6*80 38 38 12*80 20 28 20 28 80 0 80 0 80 0 80 0 80 0 80 0 28 0 28 e0 0 e0 10*0 e0 0 e0 4*0 e0 0 0 0
  //   80 4*0 e0 0 e0 e0 5*0 e0 0 80 4*0 e0 0 e0 8*0 e0 4*0 e0 0 e0 9*0 40 e0 0 0 e0 0 e0 e0 0 0 0 e0 5*0
  //   e0 60 e0 e0 0 e0 20 e0 0 e0 0 e0 0 e0 0 e0 0 e0 5*0 6*80 30 0 6*80 38 81*0 6*e0 80 80 6*e0 80 80
  //   12*e0 4*80 e0 0 e0 0 e0 0 e0 0 e0 0 e0 0 80 0 80 0 e0 6*0 e0 10*0 e0 4*0 42 12*0 e0 0 0 42 14*0 e0
  //   17*0 e0 17*0 e0 4*0 6 16*0 6*e0 80 0 6*e0 80 6*0 e0 0 e0 6*0 e0 0 0 e0 12*0 e0 4*0 e0 10*0 e0 39*0
  //   e0 e0 6*0 e0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
  //   Flags
  //   8-15
  //   contents of rom_2 (hex, n*v repeats v):
  //   256*80 256*e8 0 40 80 40 80 80 8*0 40 0 40 0 0 40 40 80 8*0 40 4*0 80 10*0 40 33*0 6*8 80 40 6*8 80
  //   40 8 8 10 10 18 18 20 20 4*0 80 80 40 40 8 0 10 0 18 40 20 40 4*0 80 40 40 40 0 80 11 80 19 0 21 0 1
  //   0 1 0 80 40 40 0 a 0 0 80 1a 80 22 0 2 0 2 0 80 40 40 0 b 0 13 0 0 80 23 0 3 0 3 0 80 40 40 40 c 0
  //   14 0 1c 80 0 80 4 0 4 0 80 40 40 40 8e 0 96 40 9e 0 a6 0 0 80 86 0 80 40 40 40 8f 0 97 0 9f 0 a7 40
  //   87 80 0 80 80 40 40 40 80 40 80 40 80 40 80 40 80 40 80 40 5*0 10 18 20 0 0 80 0 0 10 18 20 0 0 80
  //   4*0 6f 0 6f 8*0 af 0 0 0 80 ef 0 6f 8*0 6f 4*0 6f 10*0 2f 33*0 6*1 28 28 6*1 28 28 12*1 4*28 7*0 6f
  //   4*0 28 0 28 6f 80 29 0 6f 0 0 0 80 4*0 29 ef 29 0 0 80 80 2a 0 af 0 87 4*0 2a ef 2a 5*0 80 2b 0 87
  //   4*0 2b ef 2b 6*0 6f 80 2c 4*0 2c ef 2c 6f 0 80 0 ef 4*0 80 ae 0 80 ae ef ae ef 5*0 80 0 ef 0 28 80
  //   af af ef af 28 d ef 15 ef 1d ef 25 ef 5 ef 5 ef 4*0 1 2 3 4 86 87 28 0 1 2 3 4 86 87 28 4*0 40 0 80
  //   8*0 40 0 0 0 35 40 0 80 8*0 40 4*0 80 10*0 40 39*0 1 1 6*0 1 1 12*0 4*1 7*0 40 7*0 40 d 0 0 80 0 0 0
  //   5 5*0 40 0 0 0 35 15 0 0 80 7*0 40 6*0 1d 8*0 40 7*0 80 25 6*0 40 0 40 0 35 0 40 4*0 5 0 0 35 0 40 0
  //   40 5*0 35 0 40 0 0 5 0 0 40 0 c7 0 40 0 40 0 40 0 40 0 40 0 40 10*0 5 7*0 5 4*0 6e 0 6e 8*0 ae 0 0 0
  //   80 ee 0 6e 8*0 6e 4*0 6e 10*0 2e 72*0 6e 7*0 6e 0 0 0 6e 9*0 ee 0 0 0 80 0 0 0 ae 7*0 ee 15*0 ee 7*0
  //   6e 7*0 ee 0 6e 0 80 0 ee 7*0 80 0 ee 0 ee 5*0 80 0 ee 5*0 ee 0 38 0 ee 0 ee 0 ee 0 ee 0 ee 0 ee 38*0
  //   3d 80 121*0 80 0 0 0 3d 11*0 80 15*0 80 7*0 80 7*0 80 0 0 0 3d 0 80 7*0 3d 0 80 0 80 5*0 3d 0 80 5*0
  //   80 0 c7 0 80 0 80 0 80 0 80 0 80 0 80 38*0 40 35 121*0 29 15*0 2a 15*0 2b 7*0 28 7*0 2c 0 0 0 40 0
  //   35 7*0 40 0 ae 0 35 5*0 40 0 35 5*0 af 0 80 0 d 0 15 0 1d 0 25 0 5 0 5 39*0 80 175*0 80 11*0 80 7*0
  //   80 7*0 5 51*0 3d 175*0 3d 11*0 3d 7*0 3d 7*0 80 51*0 40 175*0 40 11*0 40 7*0 40 7*0 35 255*0 80
  //   255*0 3d 255*0 40 544*0 256*80 256*e8 0 0 80 0 80 80 40 40 6*0 40 0 40 0 0 0 40 80 0 40 6*0 40 0 0
  //   80 12*0 40 33*0 6*8 80 40 6*8 80 40 8 8 10 10 18 18 20 20 4*0 80 80 40 40 8 0 10 0 18 40 20 40 4*0
  //   80 40 40 40 0 80 11 0 19 80 21 0 1 0 1 0 80 40 40 40 a 0 0 80 1a 80 22 0 2 0 2 0 80 40 40 40 b 0 13
  //   0 0 80 23 0 3 0 3 0 80 40 40 0 c 0 14 0 1c 80 0 80 4 0 4 0 80 40 40 0 8e 0 96 40 9e 0 a6 0 0 80 86 0
  //   80 40 40 40 8f 0 97 40 9f 0 a7 0 87 80 0 80 80 40 40 40 80 40 80 40 80 40 80 40 80 40 80 40 5*0 10
  //   18 20 0 0 80 0 0 10 18 20 0 0 80 6*0 6f 0 6f 6*0 af 6*0 6f 80 ef 6*0 6f 0 0 6f 12*0 2f 33*0 6*1 28
  //   28 6*1 28 28 12*1 4*28 7*0 6f 4*0 28 0 28 6f 80 29 0 0 0 6f 0 80 4*0 29 ef 29 0 0 80 80 2a 0 af 0 87
  //   4*0 2a ef 2a 6f 4*0 80 2b 0 87 4*0 2b ef 2b 6*0 6f 80 2c 4*0 2c ef 2c 0 0 80 0 ef 4*0 80 ae 0 80 ae
  //   ef ae ef 0 80 0 ef 5*0 28 80 af af ef af 28 d ef 15 ef 1d ef 25 ef 5 ef 5 ef 4*0 1 2 3 4 86 87 28 0
  //   1 2 3 4 86 87 28 6*0 80 0 40 6*0 40 6*0 80 35 40 6*0 40 0 0 80 12*0 40 39*0 1 1 6*0 1 1 12*0 4*1 7*0
  //   40 7*0 40 d 4*0 80 0 5 5*0 40 0 0 0 35 15 0 0 80 7*0 40 0 40 4*0 1d 8*0 40 7*0 80 25 6*0 40 0 0 0 35
  //   0 40 4*0 5 0 0 35 0 40 0 40 0 35 0 40 6*0 5 0 0 40 0 c7 0 40 0 40 0 40 0 40 0 40 0 40 10*0 5 7*0 5
  //   6*0 6e 0 6e 6*0 ae 6*0 6e 80 ee 6*0 6e 0 0 6e 12*0 2e 72*0 6e 7*0 6e 5*0 6e 7*0 ee 0 0 0 80 0 0 0 ae
  //   7*0 ee 0 6e 13*0 ee 7*0 6e 7*0 ee 0 0 0 80 0 ee 7*0 80 0 ee 0 ee 0 80 0 ee 9*0 ee 0 38 0 ee 0 ee 0
  //   ee 0 ee 0 ee 0 ee 42*0 3d 80 117*0 80 0 0 0 3d 11*0 80 15*0 80 7*0 80 7*0 80 0 0 0 3d 0 80 7*0 3d 0
  //   80 0 80 0 3d 0 80 9*0 80 0 c7 0 80 0 80 0 80 0 80 0 80 0 80 42*0 40 35 117*0 29 15*0 2a 15*0 2b 7*0
  //   28 7*0 2c 0 0 0 40 0 35 7*0 40 0 ae 0 35 0 40 0 35 9*0 af 0 80 0 d 0 15 0 1d 0 25 0 5 0 5 43*0 80
  //   171*0 80 11*0 80 0 0 0 80 11*0 5 55*0 3d 171*0 3d 11*0 3d 0 0 0 3d 11*0 80 55*0 40 171*0 40 11*0 40
  //   0 0 0 40 11*0 35 255*0 80 255*0 3d 255*0 40 544*0 256*80 256*e8 0 0 80 0 80 80 40 40 6*0 40 0 40 80
  //   0 0 40 0 0 40 6*0 40 4*0 80 10*0 40 33*0 6*8 80 40 6*8 80 40 8 8 10 10 18 18 20 20 4*0 80 80 40 40 8
  //   0 10 0 18 40 20 40 0 40 0 40 80 0 40 0 0 80 11 0 19 80 21 0 1 0 1 0 80 40 40 0 a 0 0 80 1a 80 22 0 2
  //   0 2 0 80 40 40 0 b 0 13 0 0 80 23 0 3 0 3 0 80 40 40 40 c 0 14 0 1c 80 0 80 4 0 4 0 80 40 40 40 8e 0
  //   96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
  //   8-Bit Data Bus
  //   Z Register
  //   16-23
  //   2x32K ROM
  //   contents of rom_3 (hex, n*v repeats v):
  //   256*3 256*b 0 4 2 1 8 9 0 a 6*0 b 0 4 0 10 b 8 9 0 a 6*0 b 0 5 0 3 9 10*0 b 39*0 5 b 6*0 5 b 12*0 5
  //   5 b b 5*0 4 0 1 0 0 0 a 5 4 b 1 10 9 0 9 0 0 0 10 4*0 5 b b 0 0 10 10 9 0 9 0 c 4*0 5 b b a 4*0 10 9
  //   0 c 4*0 5 b b 4 5*0 9 10 9 4*0 5 b b 1 0 10 0 b 0 0 0 a 10 9 0 10 5 b b b 0 0 0 a 0 10 0 b 0 9 10 9
  //   5 b b b 5 b 5 b 5 b 5 b 5 b 5 b 4*0 6*c 5 e 6*c 5 6*0 20 0 a 10*0 9 0 0 20 0 a 11*0 20 10*0 1 76*0 a
  //   4*0 9 20 0 20 0 0 0 9 9*0 9 9 20 0 20 9*0 a 4*0 9 20 15*0 20 9 20 9*0 9 5*0 a 9 20 0 9 7*0 a 0 9 0 0
  //   0 a0 9 20 26*0 c 7*0 c 4*0 1 0 9 8*0 b 0 0 0 12 b 0 9 8*0 b 4*0 9 10*0 b 72*0 1 7*0 1 0 0 0 9 0 0 0
  //   40 5*0 b 0 0 0 14 0 0 0 9 7*0 b 15*0 b 7*0 9 7*0 b 0 1 0 12 0 b 7*0 12 0 b 0 b 5*0 12 0 b 5*0 b 0 0
  //   0 b 0 b 0 b 0 b 0 b 0 b 25*0 20 12*0 9 10 0 20 13*0 20 10*0 1 84*0 20 13*0 9 0 0 0 20 31*0 20 11*0 9
  //   0 10 7*0 9 0 0 0 10 5*0 9 0 10 7*0 6 50*0 2 9 121*0 7 0 0 0 4 11*0 7 15*0 7 7*0 9 7*0 7 0 0 0 2 0 9
  //   7*0 2 0 7 0 9 5*0 2 0 9 5*0 7 0 10 0 7 0 7 0 7 0 7 0 7 0 7 38*0 4 12 161*0 a0 11*0 4 0 12 7*0 4 0 0
  //   0 12 5*0 4 0 12 7*0 9 51*0 9 175*0 9 11*0 9 7*0 9 7*0 50 51*0 2 175*0 2 11*0 2 7*0 2 7*0 9 51*0 6
  //   175*0 6 11*0 6 7*0 6 7*0 12 255*0 9 255*0 2 255*0 6 544*0 256*3 256*b 0 0 2 a 8 9 4 1 6*0 b 0 4 0 0
  //   a 8 9 10 b 6*0 b 0 5 9 3 11*0 b 39*0 5 b 6*0 5 b 12*0 5 5 b b 5*0 4 0 1 0 0 0 a 5 4 b 1 10 9 0 0 0 9
  //   0 10 4*0 5 b b 4 0 10 10 9 0 9 0 c 4*0 5 b b 1 4*0 10 9 0 c 4*0 5 b b 6*0 9 10 9 4*0 5 b b a 0 10 0
  //   b 0 0 0 a 10 9 0 10 5 b b b 0 10 0 b 0 0 0 a 0 9 10 9 5 b b b 5 b 5 b 5 b 5 b 5 b 5 b 4*0 6*c 5 e
  //   6*c 5 4*0 a 0 20 13*0 a 0 20 9 10*0 20 12*0 1 76*0 a 4*0 9 20 0 0 0 20 0 9 9*0 9 9 20 0 20 14*0 9 20
  //   15*0 20 9 20 7*0 a 0 9 5*0 a 9 20 0 9 5*0 9 5*0 a 0 a0 9 20 26*0 c 7*0 c 6*0 9 0 1 6*0 b 6*0 9 12 b
  //   6*0 b 0 0 9 12*0 b 72*0 1 7*0 1 5*0 9 0 40 5*0 b 0 0 0 14 0 0 0 9 7*0 b 0 1 13*0 b 7*0 9 7*0 b 0 0 0
  //   12 0 b 7*0 12 0 b 0 b 0 12 0 b 9*0 b 0 0 0 b 0 b 0 b 0 b 0 b 0 b 25*0 20 15*0 20 9 10 9*0 20 12*0 1
  //   86*0 20 11*0 9 0 0 0 20 31*0 20 11*0 9 0 10 7*0 9 0 0 0 10 0 9 0 10 11*0 6 54*0 2 9 117*0 7 0 0 0 4
  //   11*0 7 15*0 7 7*0 9 7*0 7 0 0 0 2 0 9 7*0 2 0 7 0 9 0 2 0 9 9*0 7 0 10 0 7 0 7 0 7 0 7 0 7 0 7 42*0
  //   4 12 157*0 a0 11*0 4 0 12 7*0 4 0 0 0 12 0 4 0 12 11*0 9 55*0 9 171*0 9 11*0 9 0 0 0 9 11*0 50 55*0
  //   2 171*0 2 11*0 2 0 0 0 2 11*0 9 55*0 6 171*0 6 11*0 6 0 0 0 6 11*0 12 255*0 9 255*0 2 255*0 6 544*0
  //   256*3 256*b 0 0 2 a 8 9 4 1 6*0 b 0 4 9 0 a 8 0 10 b 6*0 b 0 5 0 3 9 10*0 b 39*0 5 b 6*0 5 b 12*0 5
  //   5 b b 5*0 4 0 1 0 4 0 1 5 0 b a 10 9 0 0 0 9 0 10 4*0 5 b b 0 0 10 10 9 0 9 0 c 4*0 5 b b a 4*0 10 9
  //   0 c 4*0 5 b b 4 5*0 9 10 9 4*0 5 b b 1 0 10 0 b 0 10 0 b 10 9 0 0 5 b b a 0 0 0 a 0 10 0 b 0 9 10 9
  //   5 b b b 5 b 5 b 5 b 5 b 5 b 5 b 4*0 6*c 5 e 6*c 5 4*0 a 0 20 11*0 20 0 a 0 0 9 12*0 20 10*0 1 80*0 a
  //   9 20 0 0 0 20 0 9 9*0 9 9 20 0 20 9*0 a 4*0 9 20 15*0 20 9 20 9*0 9 0 0 0 9 0 0 9 20 5*0 a 0 0 0 a 0
  //   9 0 0 0 a0 9 20 26*0 c 7*0 c 6*0 9 0 1 6*0 b 0 0 9 4*0 12 b 6*0 b 4*0 9 10*0 b 72*0 1 0 0 0 1 9*0 9
  //   0 40 5*0 b 0 0 0 14 0 0 0 9 7*0 b 15*0 b 7*0 9 7*0 b 0 1 0 12 0 b 0 12 0 b 5*0 b 7*0 12 0 b 5*0 b 0
  //   0 0 b 0 b 0 b 0 b 0 b 0 b 25*0 20 11*0 20 4*0 9 10 11*0 20 10*0 1 86*0 20 11*0 9 0 0 0 20 31*0 20
  //   11*0 9 0 10 0 9 0 10 13*0 9 0 10 7*0 6 54*0 2 9 117*0 7 0 0 0 4 11*0 7 15*0 7 7*0 9 7*0 7 0 0 0 2 0
  //   9 0 2 0 9 5*0 7 7*0 2 0 9 5*0 7 0 10 0 7 0 7 0 7 0 7 0 7 0 7 42*0 4 12 157*0 a0 11*0 4 0 12 0 4 0 12
  //   13*0 4 0 12 7*0 9 55*0 9 171*0 9 0 0 0 9 15*0 9 7*0 50 55*0 2 171*0 2 0 0 0 2 15*0 2 7*0 9 55*0 6
  //   171*0 6 0 0 0 6 15*0 6 7*0 12 255*0 9 255*0 2 255*0 6 544*0 256*3 256*b 0 0 2 a 8 9 4 1 6*0 b 0 4 9
  //   0 a 8 0 10 b 6*0 b 0 5 9 3 11*0 b 39*0 5 b 6*0 5 b 12*0 5 5 b b 5*0 4 0 1 0 4 0 1 5 0 b a 10 9 0 0 0
  //   9 0 10 4*0 5 b b 4 0 10 10 9 0 9 0 c 4*0 5 b b 1 4*0 10 9 0 c 4*0 5 b b 6*0 9 10 9 4*0 5 b b a 0 10
  //   0 b 0 10 0 b 10 9 0 0 5 b b a 0 10 0 b 0 0 0 a 0 9 10 9 5 b b b 5 b 5 b 5 b 5 b 5 b 5 b 4*0 6*c 5 e
  //   6*c 5 4*0 a 0 20 11*0 20 0 a 0 0 9 10*0 20 12*0 1 80*0 a 9 20 0 0 0 20 0 9 9*0 9 9 20 0 20 14*0 9 20
  //   15*0 20 9 20 7*0 a 0 9 0 0 0 9 0 0 9 20 5*0 a 0 9 5*0 a 0 a0 9 20 26*0 c 7*0 c 6*0 9 0 1 6*0 b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
  //   AT28C256 (32K)
  //   Instruction Pointer
  //   Memory Address Register
  //   L Register
  //   H Register
  //   T Register
  //   Stack Pointer
  //   HL Register
  //   2K ROM
  //   AT28C16A (2K)
  //   contents of rom_4 (hex, n*v repeats v):
  //   77 40 1 0 77 4 8 0 77 8 8 0 77 c 8 0 77 10 8 0 77 14 8 0 77 18 8 0 77 1c 8 0 77 20 8 0 77 24 8 0 77
  //   28 8 0 77 2c 8 0 77 30 8 0 77 34 8 0 77 38 8 0 77 3c 8 0 77 40 8 0 77 44 8 0 77 48 8 0 77 4c 8 0 77
  //   50 8 0 77 54 8 0 77 58 8 0 77 5c 8 0 77 60 8 0 77 64 8 0 77 68 8 0 77 6c 8 0 77 70 8 0 77 74 8 0 77
  //   78 8 0 77 7c 8 0 77 80 8 0 77 84 8 0 77 88 8 0 77 8c 8 0 77 90 8 0 77 94 8 0 77 98 8 0 77 9c 8 0 77
  //   a0 8 0 77 a4 8 0 77 a8 8 0 77 ac 8 0 77 b0 8 0 77 b4 8 0 77 b8 8 0 77 bc 8 0 77 c0 8 0 77 c4 8 0 77
  //   c8 8 0 77 cc 8 0 77 d0 8 0 77 d4 8 0 77 d8 8 0 77 dc 8 0 77 e0 8 0 77 e4 8 0 77 e8 8 0 77 ec 8 0 77
  //   f0 8 0 77 f4 8 0 77 f8 8 0 77 fc 8 0 40 1 51 1 79 1 ac 1 ad 1 ae 1 af 1 b0 1 b1 1 b2 1 b3 1 b4 1 b5
  //   1 b6 1 b7 1 b8 1 b9 1 ba 1 bb 1 bc 1 bd 1 be 1 bf 1 c0 1 c1 1 c2 1 c3 1 c4 1 c5 1 c6 1 c7 1 c8 1 2e
  //   ff ff 8e 1 9e 1f e 2 1 87 c3 51 1 77 0 9 80 92 a4 b6 91 60 60 ac 97 bc 97 91 ce 8 d0 8e 77 e0 f5 e4
  //   f5 e6 f9 9f 72 1 8a 6e 2 95 77 58 1 95 95 b7 a5 93 81 b5 92 f9 9f 84 1 f9 9f 97 1 93 b5 93 80 a4 b6
  //   60 60 f0 ce 8 d0 ac 97 bc c6 d4 b7 a5 81 b5 93 80 a4 b6 91 60 60 f0 aa b8 ce 8 d0 e4 f5 e6 95 b7 a5
  //   81 30*b5
  //   Memory Data Register
  //   2x32K RAM
  //   AS6C62256 (32K)
  //   16-Bit Address Bus
endmodule
