// Logisim project 2x4-add-sub.circ as structural Verilog: 1 circuit, main circuit main
module main (
  input  Z_TO_DATA,
  input  FLAGS,
  input  FLAGS_TO_DATA,
  input  [7:0] in_4,
  input  DATA_TO_FLAGS,
  input  [7:0] X,
  input  in_7,
  input  CARRY,
  input  SUB,
  input  [7:0] Y,
  output [7:0] Z,
  output [7:0] DATA,
  output ZF,
  output CF,
  output [7:0] _C_Z
);

  wire adder_1_cout, adder_2_cout, CLK, or_1_out, RST, xor_1_out;
  wire [1:0] nor_1_out;
  wire [3:0] bit_extender_1_out, xor_2_out, xor_4_out;
  wire [7:0] multiplexer_1_out, register_1_q;

  Button u_CLK (.out(CLK));
  Button u_RST (.out(RST));
  assign bit_extender_1_out = {{3{SUB}}, SUB};  // Bit_Extender bit_extender_1
  xor xor_1 (xor_1_out, CARRY, SUB);
  assign xor_2_out = bit_extender_1_out ^ Y[7:4];  // XOR_Gate xor_2, 4 bits wide
  Adder #(.width(4)) adder_1 (.a(X[7:4]), .b(xor_2_out), .out(Z[7:4]), .cin(adder_2_cout), .cout(adder_1_cout));
  xor xor_3 (nor_1_out[1], adder_1_cout, SUB);
  assign xor_4_out = bit_extender_1_out ^ Y[3:0];  // XOR_Gate xor_4, 4 bits wide
  Adder #(.width(4)) adder_2 (.a(X[3:0]), .b(xor_4_out), .out(Z[3:0]), .cin(xor_1_out), .cout(adder_2_cout));
  nor nor_1 (nor_1_out[0], Z[0], Z[1], Z[2], Z[3], Z[4], Z[5], Z[6], Z[7]);
  Multiplexer #(.width(8), .enable("false")) multiplexer_1 (
    .in0({{6{1'b0}}, register_1_q[1:0]}), .in1(DATA), .out(multiplexer_1_out), .sel(DATA_TO_FLAGS));
  or or_1 (or_1_out, DATA_TO_FLAGS, FLAGS);
  assign DATA = Z_TO_DATA ? Z : 8'bz;  // Controlled_Buffer controlled_buffer_1
  Register register_1 (.D({{6{1'b0}}, nor_1_out}), .en(Z_TO_DATA), .Q(register_1_q), .clk(CLK));  // open: clr
  assign DATA = FLAGS_TO_DATA ? _C_Z : 8'bz;  // Controlled_Buffer controlled_buffer_2
  Register register_2 (.D(multiplexer_1_out), .en(or_1_out), .Q(_C_Z), .clk(CLK), .clr(RST));
  assign DATA = in_7 ? in_4 : 8'bz;  // Controlled_Buffer controlled_buffer_3

  assign CF = _C_Z[1];
  assign ZF = _C_Z[0];
endmodule
