// Logisim project add-sub.circ as structural Verilog: 1 circuit, main circuit main
module main (
  input  CARRY,
  input  [7:0] A,
  input  [7:0] B,
  input  SUB,
  input  [3:0] in_5,
  input  [3:0] in_6,
  input  SUB_2,
  input  [3:0] in_8,
  input  [3:0] in_9,
  output [7:0] out_10,
  output CARRY_2,
  output [3:0] out_12,
  output [3:0] out_13,
  output CARRY_3
);

  wire adder_1_cout, adder_2_cout, adder_3_cout, xor_1_out;
  wire [3:0] bit_extender_2_out, xor_3_out, xor_6_out;
  wire [7:0] bit_extender_1_out, xor_2_out;

  assign bit_extender_1_out = {{7{SUB}}, SUB};  // Bit_Extender bit_extender_1
  xor xor_1 (xor_1_out, CARRY, SUB);
  assign xor_2_out = B ^ bit_extender_1_out;  // XOR_Gate xor_2, 8 bits wide
  assign bit_extender_2_out = {{3{SUB_2}}, SUB_2};  // Bit_Extender bit_extender_2
  Adder adder_1 (.a(A), .b(xor_2_out), .out(out_10), .cin(xor_1_out), .cout(adder_1_cout));
  assign xor_3_out = bit_extender_2_out ^ in_8;  // XOR_Gate xor_3, 4 bits wide
  xor xor_4 (CARRY_2, adder_1_cout, SUB);
  Adder #(.width(4)) adder_2 (.a(in_5), .b(xor_3_out), .out(out_12), .cin(adder_3_cout), .cout(adder_2_cout));
  xor xor_5 (CARRY_3, adder_2_cout, SUB_2);
  assign xor_6_out = bit_extender_2_out ^ in_9;  // XOR_Gate xor_6, 4 bits wide
  Adder #(.width(4)) adder_3 (.a(in_6), .b(xor_6_out), .out(out_13), .cin(SUB_2), .cout(adder_3_cout));
endmodule
