// Logisim project bus-transfer.circ as structural Verilog: 1 circuit, main circuit main
module main (
  input  in_1,
  input  in_2,
  input  [7:0] in_3,
  input  [15:0] in_4,
  input  in_5,
  input  in_6,
  input  in_7,
  input  in_8,
  input  in_9,
  input  in_10,
  output [7:0] out_11,
  output [15:0] out_12
);

  wire and_1_out, and_2_out, CLK, or_1_out, or_2_out, RST;
  wire [7:0] register_1_q, register_1_q_2;

  assign out_11 = in_5 ? in_3 : 8'bz;  // Controlled_Buffer controlled_buffer_1
  assign out_12[7:0] = in_7 ? out_11 : 8'bz;  // Controlled_Buffer controlled_buffer_2
  assign out_11 = in_8 ? out_12[7:0] : 8'bz;  // Controlled_Buffer controlled_buffer_3
  Button button_1 (.out(CLK));
  Button button_2 (.out(RST));
  Register #(.width(16)) register_1 (.D(out_12), .en(in_1), .Q({register_1_q_2, register_1_q}), .clk(CLK), .clr(RST));
  and and_1 (and_1_out, in_10, in_1);
  and and_2 (and_2_out, in_1, in_7);
  assign out_12[7:0] = or_1_out ? register_1_q : 8'bz;  // Controlled_Buffer controlled_buffer_4
  assign out_12[15:8] = or_2_out ? register_1_q_2 : 8'bz;  // Controlled_Buffer controlled_buffer_5
  or or_1 (or_1_out, and_1_out, in_2);
  or or_2 (or_2_out, in_2, and_2_out);
  assign out_11 = in_9 ? out_12[15:8] : 8'bz;  // Controlled_Buffer controlled_buffer_6
  assign out_12 = in_6 ? in_4 : 16'bz;  // Controlled_Buffer controlled_buffer_7
  assign out_12[15:8] = in_10 ? out_11 : 8'bz;  // Controlled_Buffer controlled_buffer_8

  // Other names for the same wires on the sheet: A_TO_ADDR = in_2; ADDR_HI_TO_DATA = in_9; ADDR_LO_TO_DATA = in_8;
  //   ADDR_TO_A = in_1; DATA_TO_ADDR_HI = in_10; DATA_TO_ADDR_LO = in_7
endmodule
