// Logisim project digits.circ as structural Verilog: 1 circuit, main circuit main
module main (
  output [3:0] out_1,
  output [7:0] out_2
);

  wire clock_1_out;

  Counter #(.width(4), .max('hf)) counter_1 (
    .load(1'b0), .count(1'b1), .Q(out_1), .clk(clock_1_out));  // open: D, carry, clr
  Clock clock_1 (.out(clock_1_out));
  ROM #(.addrWidth(4)) rom_1 (.addr(out_1), .data(out_2), .sel(1'b1));
  _7_Segment_Display u_7_segment_display_1 (
    .g(out_2[1]), .f(out_2[2]), .a(out_2[7]), .b(out_2[6]), .e(out_2[3]), .d(out_2[4]), .c(out_2[5]),
    .dp(out_2[0]));

  // Notes on the sheet:
  //   contents of rom_1 (hex, n*v repeats v):
  //   fc 60 da f2 66 b6 be e0 fe f6 ee 3e 9c 7a 9e 8e
endmodule
