// Logisim project ram-rom.circ as structural Verilog: 1 circuit, main circuit main
module main (
  input  in_1,
  input  in_2,
  input  [7:0] in_3,
  input  in_4,
  input  [15:0] in_5,
  output [7:0] out_6,
  output [7:0] out_7
);

  wire and_1_out, CLK, decoder_1_out0, decoder_1_out1, nor_1_out, not_1_out, not_2_out, not_3_out, xor_1_out;
  wire [7:0] rom_4_data;

  RAM #(.addrWidth(15)) ram_1 ();  // open: addr, data, sel, clk, ld, clr
  ROM #(.addrWidth(11)) rom_1 ();  // open: addr, data, sel
  assign out_6 = in_4 ? in_3 : 8'bz;  // Controlled_Buffer controlled_buffer_1
  assign out_6 = in_2 ? out_7 : 8'bz;  // Controlled_Buffer controlled_buffer_2
  RAM #(.addrWidth(17)) ram_2 ();  // open: addr, data, sel, clk, ld, clr
  ROM #(.addrWidth(13)) rom_2 ();  // open: addr, data, sel
  RAM #(.addrWidth(19)) ram_3 ();  // open: addr, data, sel, clk, ld, clr
  ROM #(.addrWidth(15)) rom_3 ();  // open: addr, data, sel
  Decoder #(.disabled(0), .enable("false")) decoder_1 (.out0(decoder_1_out0), .out1(decoder_1_out1), .sel(in_5[15]));
  nor nor_1 (nor_1_out, in_5[11], in_5[12], in_5[13], in_5[14], in_5[15]);
  not not_1 (not_1_out, nor_1_out);
  xor xor_1 (xor_1_out, nor_1_out, decoder_1_out0);
  and and_1 (and_1_out, not_1_out, in_1);
  not not_2 (not_2_out, and_1_out);
  assign out_7 = and_1_out ? out_6 : 8'bz;  // Controlled_Buffer controlled_buffer_3
  ROM #(.addrWidth(11)) rom_4 (.addr(in_5[10:0]), .data(rom_4_data), .sel(nor_1_out));
  not not_3 (not_3_out, in_1);
  assign out_7 = not_3_out ? rom_4_data : 8'bz;  // Controlled_Buffer controlled_buffer_4
  RAM #(.addrWidth(15)) ram_4 (
    .addr(in_5[14:0]), .data(out_7), .sel(xor_1_out), .clk(CLK), .ld(not_2_out));  // open: clr
  RAM #(.addrWidth(15)) ram_5 (
    .addr(in_5[14:0]), .data(out_7), .sel(decoder_1_out1), .clk(CLK), .ld(not_2_out));  // open: clr
  Button button_1 (.out(CLK));

  // Other names for the same wires on the sheet: DATA_TO_MDR = in_1; MDR_TO_DATA = in_2

  // Notes on the sheet:
  //   AS6C62256 (32K)
  //   AT28C16A (2K)
  //   AS6C1008 (128K)
  //   AT28C64B (8K)
  //   AS6C4008 (512K)
  //   AT28C256 (32K)
  //   contents of rom_4 (hex, n*v repeats v):
  //   aa
endmodule
